# Fritzing sketch Arduino-DRV8825 (saved by Fritzing 0.9.3b)
breadboards: 1

parts:
  元件1 = Arduino Mega 2560 (Rev3)
  DRV_1 = DRV 8825 Stepper Motor Carrier, High Current [part_number="DRV 8825"]
  Power_plug1 = Power plug
  M1 = Stepper Motor - Bipolar
  C1 = Electrolytic Capacitor [capacitance=1µF package="100 mil [THT, electrolytic]"]

nets:
  N1: 元件1.GND, DRV_1.GROUND_LOG
  N2: 元件1.5V, DRV_1.RESET, DRV_1.SLEEP, DRV_1.VOLTAGE_DD
  N3: 元件1.D2_PWM, DRV_1.DIRECTION
  N4: 元件1.D3_PWM, DRV_1.STEP
  N5: DRV_1.VOLTAGE_ST/_MT, Power_plug1.VCC, C1.+
  N6: DRV_1.GROUND_ST/_MT, Power_plug1.GND, C1.-
  N7: DRV_1.OUT_2B, M1.A
  N8: DRV_1.OUT_2A, M1.C
  N9: DRV_1.OUT_1A, M1.B
  N10: DRV_1.OUT_1B, M1.D
