# Fritzing sketch Arduino-Mega-Mega-Sketch (saved by Fritzing 0.9.3b)

parts:
  元件1 = Arduino Mega 2560 (Rev3)
  C1 = Electrolytic Capacitor [capacitance=1µF package="100 mil [THT, electrolytic]"]
  元件2 = Arduino Mega 2560 (Rev3)

nets:
  N1: 元件1.RESET, C1.+
  5V: 元件1.5V, 元件2.5V
  GND: 元件1.GND, C1.-, 元件2.GND
