# Fritzing sketch Arduino-Mega-UNO-Sketch (saved by Fritzing 0.9.3b)

parts:
  元件1 = Arduino Mega 2560 (Rev3)
  元件2 = Arduino Uno (Rev3)
  C1 = Electrolytic Capacitor [capacitance=1µF package="100 mil [THT, electrolytic]"]

nets:
  N1: 元件1.D10_PWM, 元件2.RESET
  N2: 元件1.RESET, C1.+
  5V: 元件1.5V, 元件2.5V
  GND: 元件1.GND, 元件2.GND, C1.-
  N3: 元件1.D50, 元件2.D12/MISO
  N4: 元件1.D51, 元件2.D11_PWM/MOSI
  N5: 元件1.D52, 元件2.D13/SCK
